# Fritzing sketch ESP32New (saved by Fritzing 0.9.3b)

parts:
  Chirp!_Soil_Moisture_Sensor1 = Chirp! Soil Moisture Sensor v2.7.3
  U1 = LIPO-110mAh [package=lipo-110]
  MCU1 = Wemos Lolin32lite
  Part1 = ws2812b [package="smd 2812b"]  # not connected
  Part2 = ws2812b [package="smd 2812b"]  # not connected
  Part3 = ws2812b [package="smd 2812b"]
  R1 = Resistor [tolerance=±5% resistance=10k package="1206 [SMD]"]
  R2 = Resistor [tolerance=±5% resistance=10k package="1206 [SMD]"]
  R3 = Resistor [tolerance=±5% resistance=10k package="1206 [SMD]"]

nets:
  N1: Chirp!_Soil_Moisture_Sensor1.Pin_1, MCU1.pin_28, Part3.VSS
  N2: Chirp!_Soil_Moisture_Sensor1.pin_2, R3.Pin_0
  N3: Chirp!_Soil_Moisture_Sensor1.pin_3, R2.Pin_0
  N4: Chirp!_Soil_Moisture_Sensor1.pin_5, MCU1.pin_13, Part3.VDD
  N5: U1.+, MCU1.pin_15
  N6: U1.-, MCU1.pin_14
  N7: MCU1.pin_17, R2.Pin_1
  N8: MCU1.pin_18, R3.Pin_1
  N9: MCU1.pin_20, R1.Pin_0
  N10: Part3.DIN, R1.Pin_1

custom parts:
  Wemos Lolin32lite: Wemos Lolinlite32 wifi and blue tooth board based on the ESP-32 cpu, digital I/Os 19, analog inputs 6, clock 240mhz, Flash 4Mbytes, lipo battery charger (500ma connection broken out on breadboard but not pcb), usb.
